# Fritzing sketch telcommande (saved by Fritzing 0.9.3b)
circuit board: 9.26836cm x 9.72268cm
breadboards: 1

parts:
  S1 = SWITCH-MOMENTARY-2 [package=tactile-pth-12mm]
  S2 = SWITCH-MOMENTARY-2 [package=tactile-pth-12mm]
  S3 = SWITCH-MOMENTARY-2 [package=tactile-pth-12mm]
  S4 = SWITCH-MOMENTARY-2 [package=tactile-pth-12mm]
  S5 = SWITCH-MOMENTARY-2 [package=tactile-pth-12mm]
  S6 = SWITCH-MOMENTARY-2 [package=tactile-pth-12mm]
  S7 = SWITCH-MOMENTARY-2 [package=tactile-pth-12mm]
  S8 = SWITCH-MOMENTARY-2 [package=tactile-pth-12mm]
  S9 = SWITCH-MOMENTARY-2 [package=tactile-pth-12mm]
  S10 = SWITCH-MOMENTARY-2 [package=tactile-pth-12mm]
  S11 = SWITCH-MOMENTARY-2 [package=tactile-pth-12mm]
  S12 = SWITCH-MOMENTARY-2 [package=tactile-pth-12mm]
  S13 = SWITCH-MOMENTARY-2 [package=tactile-pth-12mm]
  Composant1 = Arduino Nano (Rev3.0)
  S14 = SWITCH-MOMENTARY-2 [package=tactile-pth-12mm]
  R1 = Resistor [tolerance=±5% resistance=220 package=THT]
  R2 = Resistor [tolerance=±5% resistance=220 package=THT]
  R3 = Resistor [tolerance=±5% resistance=220 package=THT]
  R4 = Resistor [tolerance=±5% resistance=220 package=THT]
  R5 = Resistor [tolerance=±5% resistance=220 package=THT]
  R6 = Resistor [tolerance=±5% resistance=220 package=THT]
  R7 = Resistor [tolerance=±5% resistance=220 package=THT]
  R9 = Resistor [tolerance=±5% resistance=220 package=THT]
  R10 = Resistor [tolerance=±5% resistance=220 package=THT]
  R11 = Resistor [tolerance=±5% resistance=220 package=THT]
  R13 = Resistor [tolerance=±5% resistance=220 package=THT]
  R14 = Resistor [tolerance=±5% resistance=220 package=THT]
  R16 = Resistor [tolerance=±5% resistance=220 package=THT]
  R17 = Resistor [tolerance=±5% resistance=220 package=THT]
  R18 = Resistor [tolerance=±5% resistance=220 package=THT]
  R19 = Resistor [tolerance=±5% resistance=220 package=THT]
  R20 = Resistor [tolerance=±5% resistance=220 package=THT]
  R21 = Resistor [tolerance=±5% resistance=220 package=THT]
  R22 = Resistor [tolerance=±5% resistance=220 package=THT]
  R23 = Resistor [tolerance=±5% resistance=220 package=THT]
  JP1 = Header 2 [package=molex-1x2_lock]
  JP2 = Header 4 [package=screwterminal-3.5mm-4_lock]
  R24 = Resistor [tolerance=±5% resistance=220 package=THT]
  R25 = Resistor [tolerance=±5% resistance=220 package=THT]

nets:
  N1: S1.1, Composant1.D12/MISO, R20.Pin_0, R21.Pin_0
  N2: S1.2, S14.2
  N3: S2.1, Composant1.D2
  N4: S2.2, S7.2, Composant1.5V, JP2.3
  N5: S3.1, R24.Pin_0
  N6: S3.2, S4.2, S11.2, S12.2, S13.2
  N7: S4.1, R10.Pin_1
  N8: S5.1, R5.Pin_1
  N9: S5.2, S8.2
  N10: S6.1, R6.Pin_0
  N11: S7.1, Composant1.D9, R22.Pin_1, R23.Pin_1
  N12: S8.1, Composant1.D6
  N13: S9.1, R13.Pin_0, R14.Pin_0
  N14: S10.1, R16.Pin_0, R19.Pin_0
  N15: S11.1, Composant1.A3
  N16: S12.1, Composant1.A2
  N17: S13.1, Composant1.A1
  N18: Composant1.GND, R1.Pin_0, R2.Pin_0, R4.Pin_1, R5.Pin_0, R6.Pin_1, R7.Pin_0, JP1.2
  N19: Composant1.D3, R25.Pin_1
  N20: Composant1.A5, JP2.2
  N21: Composant1.A4, JP2.1
  N22: S14.1, R17.Pin_0, R18.Pin_0
  N23: R1.Pin_1, JP2.4
  N24: R2.Pin_1, R3.Pin_0
  N25: R3.Pin_1, R9.Pin_0, R11.Pin_1, R13.Pin_1, R14.Pin_1, R16.Pin_1, R17.Pin_1, R18.Pin_1, R19.Pin_1, R20.Pin_1, R21.Pin_1, R22.Pin_0, R23.Pin_0
  N26: R9.Pin_1, R24.Pin_1
  N27: R10.Pin_0, R11.Pin_0
  N28: JP1.1, R25.Pin_0
